# Fritzing sketch tcc_deteccao_zero (saved by Fritzing 0.9.3b)
breadboards: 1

parts:
  D1 = Rectifier Diode [part_number=1N4001 package="300 mil [THT]"]
  D2 = Rectifier Diode [part_number=1N4001 package="300 mil [THT]"]
  D3 = Rectifier Diode [part_number=1N4001 package="300 mil [THT]"]
  D4 = Rectifier Diode [part_number=1N4001 package="300 mil [THT]"]
  U1 = Optocoupler [package=THT]
  R1 = Resistor [tolerance=±5% resistance=3.3k package=THT]
  R2 = Resistor [tolerance=±5% resistance=10k package=THT]
  U2 = SN74LS14N [package="DIP14 [THT]"]
  U3 = Transformer [package=transformer]
  U4 = MOC3031-M [package=dil06]  # not connected
  U3_2 = ESP8266 NodeMCU LoLin module
  SCR1 = SCR [package="TO220 [THT]"]  # not connected
  Fuse1 = Fuse with Handler [part_number=Htc-15m]  # not connected
  V1 = AC Power [voltage=220V frequency=60]
  U6 = POT [package=pot_mammoth]
  V2 = AC Power [voltage=220V frequency=60]  # not connected

nets:
  N1: D1.cathode, D4.cathode, R1.Pin_0
  N2: D1.anode, D2.cathode, U3.3
  N3: D2.anode, D3.anode, U1.Pin_2
  N4: D3.cathode, D4.anode, U3.4
  N5: U1.Pin_1, R1.Pin_1
  GND: U1.Pin_4, U2.GND, U3_2.GND, U6.A
  N6: U1.Pin_5, R2.Pin_0, U2.3A, U2.3Y
  5V: R2.Pin_1, U2.VCC, U3_2.Vin
  N7: U2.1A, U2.1Y, U2.2Y
  N8: U2.2A, U3_2.D2
  N9: U3.1, V1.V+
  N10: U3.2, V1.V-
  N11: U3_2.3V3, U6.E
  N12: U3_2.A0, U6.S

custom parts:
  ESP8266 NodeMCU LoLin module: ESP8266 based NodeMCU
  SCR: Silicon Controlled Rectifier - TO220
